# Fritzing sketch menu_RPi (saved by Fritzing 0.9.3b)

parts:
  Raspberry_Pi1 = Raspberry Pi Zero
  OLED_I2C1 = OLED 128x64 I2C Monochrome Display
  RE1 = KY-040 Rotary encoder [package=THT]

nets:
  3V3: Raspberry_Pi1.3v3, OLED_I2C1.VDD
  N1: Raspberry_Pi1.GPIO2, OLED_I2C1.SDA
  N2: Raspberry_Pi1.GPIO3, OLED_I2C1.SCK
  GND: Raspberry_Pi1.GND, OLED_I2C1.GND, RE1.GND
  N3: Raspberry_Pi1.GIPO18, RE1.CLK
  N4: Raspberry_Pi1.GIPO15, RE1.DT
  N5: Raspberry_Pi1.GIPO14, RE1.SW
  5V: Raspberry_Pi1.5V, RE1.Vcc

custom parts:
  Raspberry Pi Zero: The Raspberry Pi Zero is the latest single board computer to be released by the Raspberry Pi Foundation. It is the entry level model Raspberry Pi perfect for hobbyists, makers and industrial engineers looking to create solutions where small size and low power consumption are important. This is especially relevant for applications in the wearables space as well as up and coming applications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
  KY-040 Rotary encoder: KY-040 Rotary Encoder with switch on breakout borad from AZ Delivery
